# Fritzing sketch rfid (saved by Fritzing 0.9.3b)
breadboards: 1

parts:
  LED1 = RGB LED (com. cathode, rgb) [package="5 mm [THT]"]
  J1 = Basic Servo
  부품1 = Arduino Uno (Rev3)
  R1 = Resistor [tolerance=±5% resistance=220 package=THT]
  U1 = RFID RC522 SIP - 8 pins [chip_label="RFID RC522" package="SIP (Single Inline) [THT]"]

nets:
  N1: LED1.red_anode, 부품1.D7
  N2: LED1.common_cathode, R1.Pin_1
  N3: LED1.green_anode, 부품1.D6_PWM
  GND: J1.gnd, 부품1.GND, R1.Pin_0, U1.GND
  VCC: J1.vcc, 부품1.5V
  N4: J1.pulse, 부품1.D8
  N5: 부품1.D9_PWM, U1.RST
  N6: 부품1.D10_PWM/SS, U1.IRQ
  N7: 부품1.D11_PWM/MOSI, U1.SCK
  N8: 부품1.D12/MISO, U1.MOSI
  N9: 부품1.D13/SCK, U1.NSS
  3V3: 부품1.3V3, U1.VCC

custom parts:
  RFID RC522 SIP - 8 pins: A SIP stand-in part for RFID RC522 . With 8 pins on a 300 mil single inline package (SIP) footprint.
